// Logisim project ECE200_project3.circ as structural Verilog: 1 circuit, main circuit main
module main (
  input  in_1,
  input  X2,
  input  X1,
  input  in_4,
  input  X0,
  input  in_6,
  output [1:0] out_7
);

  wire and_2_out, and_3_out, and_4_out, and_5_out, multiplexer_1_out, multiplexer_2_out, not_1_out,
       not_2_out, or_1_out, or_2_out, Y1, Y2;

  and and_1 (Y2, ~X2, ~X1);  // AND_Gate
  and and_2 (and_2_out, X2, ~X1);  // AND_Gate
  and and_3 (and_3_out, ~X2, X1);  // AND_Gate
  and and_4 (and_4_out, out_7[1], ~X2, X1);  // AND_Gate
  and and_5 (and_5_out, out_7[1], out_7[0], X2, ~X1);  // AND_Gate
  and and_6 (Y1, ~X2, ~X1, X0);  // AND_Gate
  not not_1 (not_1_out, X0);
  or or_1 (or_1_out, and_2_out, not_1_out, and_3_out);
  or or_2 (or_2_out, and_4_out, and_5_out);
  // Probe on or_2_out
  not not_2 (not_2_out, X1);
  Multiplexer #(.select(2)) multiplexer_1 (
    .in0(in_1), .in1(Y1), .in2(not_2_out), .in3(Y2), .out(multiplexer_1_out), .sel(out_7));
  Multiplexer #(.select(2)) multiplexer_2 (
    .in0(Y1), .in1(or_1_out), .in2(Y1), .in3(Y2), .out(multiplexer_2_out), .sel(out_7));
  D_Flip_Flop d_ff_1 (.D(multiplexer_1_out), .clk(in_6), .Q(out_7[1]), .reset(in_4));  // open: Qn, preset
  D_Flip_Flop d_ff_2 (.D(multiplexer_2_out), .clk(in_6), .Q(out_7[0]));  // open: Qn, preset, reset

  // Other names for the same wires on the sheet: S0 = out_7[0]; S1 = out_7[1]
endmodule
